// Logisim project SR AND D FILP_FLOP.circ as structural Verilog: 1 circuit, main circuit main
module main (
  input  S,
  input  R,
  input  in_3
);

  wire and_1_out, and_2_out, and_3_out, and_4_out, clock_1_out, clock_2_out, nor_1_out, nor_2_out, nor_3_out,
       nor_4_out, not_1_out;

  Clock clock_1 (.out(clock_1_out));
  Clock clock_2 (.out(clock_2_out));
  not not_1 (not_1_out, in_3);
  and and_1 (and_1_out, not_1_out, clock_1_out);
  and and_2 (and_2_out, clock_1_out, in_3);
  and and_3 (and_3_out, S, clock_2_out);
  and and_4 (and_4_out, clock_2_out, R);
  nor nor_1 (nor_1_out, and_3_out, nor_2_out);
  nor nor_2 (nor_2_out, nor_1_out, and_4_out);
  nor nor_3 (nor_3_out, and_1_out, nor_4_out);
  nor nor_4 (nor_4_out, nor_3_out, and_2_out);
  LED led_1 (.in(nor_1_out));
  LED led_2 (.in(nor_2_out));
  LED led_3 (.in(nor_3_out));
  LED led_4 (.in(nor_4_out));

  // Notes on the sheet:
  //   SR FILP_FOLP
  //   D FILP_FOLP
  //   Q'
  //   Q
endmodule
