// Logisim project T Flip Flop.circ as structural Verilog: 1 circuit, main circuit main
module main (
  input  in_1
);

  wire and_1_out, and_2_out, clock_1_out, nor_1_out, nor_2_out;

  Clock clock_1 (.out(clock_1_out));
  and and_1 (and_1_out, nor_1_out, in_1, clock_1_out);
  and and_2 (and_2_out, clock_1_out, in_1, nor_2_out);
  nor nor_1 (nor_1_out, and_1_out, nor_2_out);
  nor nor_2 (nor_2_out, nor_1_out, and_2_out);
  LED led_1 (.in(nor_1_out));
  LED led_2 (.in(nor_2_out));

  // Notes on the sheet:
  //   T Flip Flop
endmodule
